# Fritzing sketch CHIP_TICKER (saved by Fritzing 0.9.3b)

parts:
  C_H_I_P_1 = Next Thing Co. C.H.I.P
  R1 = Resistor [tolerance=±5% resistance=330 package=THT]
  R2 = Resistor [tolerance=±5% resistance=330 package=THT]
  R3 = Resistor [tolerance=±5% resistance=330 package=THT]
  R4 = Resistor [tolerance=±5% resistance=330 package=THT]

nets:
  N1: C_H_I_P_1.LCD-D4, R1.Pin_0
  N2: C_H_I_P_1.LCD-D6, R2.Pin_0
  N3: C_H_I_P_1.LCD-D5, R4.Pin_0
  N4: C_H_I_P_1.LCD-D7, R3.Pin_1

notes:
  R1 = R2 = R3 = R4 = 330 OHM
